// Logisim project Codigologisim.circ as structural Verilog: 23 circuits, main circuit Flip Flop D e JK
module Flip_Flop_D_e_JK (
  input  Clock,
  input  D,
  input  Preset,
  input  Clear,
  input  Enable,
  input  J,
  input  Clock_2,
  input  K,
  input  Preset_2,
  input  Enable_2,
  input  Clear_2,
  output \Saída ,
  output Complemento,
  output \Saída_2 ,
  output Complemento_2
);

  D_Flip_Flop d_ff_1 (.clk(Clock), .D(D), .Q(\Saída ), .Qn(Complemento), .preset(Preset), .en(Enable), .reset(Clear));
  J_K_Flip_Flop j_k_ff_1 (
    .J(J), .clk(Clock_2), .K(K), .Q(\Saída_2 ), .Qn(Complemento_2), .preset(Preset_2), .en(Enable_2),
    .reset(Clear_2));
endmodule

module Multiplexador (
  input  _0,
  input  _1,
  input  _2,
  input  _3,
  input  [1:0] select,
  output \saída ,
  output complemento
);

  Multiplexer #(.select(2)) multiplexer_1 (
    .in0(_0), .in1(_1), .in2(_2), .in3(_3), .out(\saída ), .sel(select), .en(complemento));
endmodule

module XOR (
  input  J,
  input  K,
  output out_3
);

  wire and_0_out, and_1_out, not_1_out, not_2_out;

  not not_1 (not_1_out, J);
  not not_2 (not_2_out, K);
  and and_0 (and_0_out, not_1_out, K);
  and and_1 (and_1_out, J, not_2_out);
  or \or  (out_3, and_0_out, and_1_out);
endmodule

module Somador_8_bits_com_4 (
  input  inteiro,
  input  in_2,
  input  in_3,
  input  in_4,
  input  in_5,
  input  in_6,
  input  in_7,
  input  in_8,
  input  in_9,
  input  in_10,
  input  in_11,
  input  in_12,
  input  in_13,
  input  in_14,
  input  in_15,
  input  in_16,
  input  in_17,
  input  overflow
);

  wire adder_2_cout, adder_3_cout, adder_4_cout, adder_5_cout, adder_6_cout, adder_7_cout, adder_8_cout;
  wire [3:0] adder_4_out, adder_8_out;

  Adder #(.width(1)) adder_1 (.a(in_10), .b(in_2), .out(adder_4_out[3]), .cin(adder_2_cout), .cout(overflow));
  Adder #(.width(1)) adder_2 (.a(in_11), .b(in_3), .out(adder_4_out[2]), .cin(adder_3_cout), .cout(adder_2_cout));
  Hex_Digit_Display hex_digit_display_1 (.value(adder_4_out));  // open: dp
  Adder #(.width(1)) adder_3 (.a(in_12), .b(in_4), .out(adder_4_out[1]), .cin(adder_4_cout), .cout(adder_3_cout));
  Adder #(.width(1)) adder_4 (.a(in_13), .b(in_5), .out(adder_4_out[0]), .cin(adder_5_cout), .cout(adder_4_cout));
  Adder #(.width(1)) adder_5 (.a(in_14), .b(in_6), .out(adder_8_out[3]), .cin(adder_6_cout), .cout(adder_5_cout));
  Adder #(.width(1)) adder_6 (.a(in_15), .b(in_7), .out(adder_8_out[2]), .cin(adder_7_cout), .cout(adder_6_cout));
  Hex_Digit_Display hex_digit_display_2 (.value(adder_8_out));  // open: dp
  Adder #(.width(1)) adder_7 (.a(in_16), .b(in_8), .out(adder_8_out[1]), .cin(adder_8_cout), .cout(adder_7_cout));
  Adder #(.width(1)) adder_8 (.a(in_17), .b(in_9), .out(adder_8_out[0]), .cin(inteiro), .cout(adder_8_cout));
endmodule

module RAM_1x8 (
  input  [1:0] CLOCK,
  input  [3:0] Entrada,
  input  [1:0] in_3,
  input  Limpar,
  output [3:0] Saida
);

  wire chave_1_out_2, chave_1_out_3, chave_1_out_4, chave_1_out_5;
  wire [3:0] ram_1x4_1_p4, ram_1x4_2_saida, ram_1x4_3_saida, ram_1x4_4_p4;

  Chave chave_1 (
    .in_1(in_3), .out_2(chave_1_out_2), .out_3(chave_1_out_3), .out_4(chave_1_out_4), .out_5(chave_1_out_5));
  // RAM_1x4 ram_1x4_1: pin names not known; wires that end beside it: Entrada, CLOCK, chave_1_out_2, ram_1x4_1_p4, Limpar
  RAM_1x4 ram_1x4_2 (.Entrada(Entrada), .clock(CLOCK), .Ligar(chave_1_out_4), .Limpar(Limpar), .Saida(ram_1x4_2_saida));
  RAM_1x4 ram_1x4_3 (.Entrada(Entrada), .clock(CLOCK), .Ligar(chave_1_out_3), .Limpar(Limpar), .Saida(ram_1x4_3_saida));
  // RAM_1x4 ram_1x4_4: pin names not known; wires that end beside it: Entrada, CLOCK, chave_1_out_5, ram_1x4_4_p4, Limpar
  assign Saida = ram_1x4_3_saida | ram_1x4_1_p4 | ram_1x4_2_saida | ram_1x4_4_p4;  // OR_Gate or_1, 4 bits wide
endmodule

module RAM_1x4 (
  input  [1:0] clock,
  input  [3:0] Entrada,
  input  Ligar,
  input  Limpar,
  output [3:0] Saida
);

  RAM_1x2 ram_1x2_1 (.CLK(Entrada[0]), .in_1(clock), .Ligar(Ligar), .Limpar(Limpar), .out_5(Saida[1:0]));
  RAM_1x2 ram_1x2_2 (.CLK(Entrada[2]), .in_1(clock), .Ligar(Ligar), .Limpar(Limpar), .out_5(Saida[3:2]));
endmodule

module RAM_1x2 (
  input  [1:0] in_1,
  input  CLK,
  input  Ligar,
  input  Limpar,
  output [1:0] out_5
);

  wire j_k_ff_1_q, j_k_ff_2_q, not_1_out, not_2_out;

  not not_1 (not_1_out, in_1[1]);
  J_K_Flip_Flop j_k_ff_1 (
    .J(in_1[1]), .clk(CLK), .K(not_1_out), .Q(j_k_ff_1_q), .en(Ligar), .reset(Limpar));  // open: Qn, preset
  J_K_Flip_Flop j_k_ff_2 (
    .J(in_1[0]), .clk(CLK), .K(not_2_out), .Q(j_k_ff_2_q), .en(Ligar), .reset(Limpar));  // open: Qn, preset
  not not_2 (not_2_out, in_1[0]);
  and and_1 (out_5[0], Ligar, j_k_ff_2_q);
  and and_2 (out_5[1], Ligar, j_k_ff_1_q);
endmodule

module Chave (
  input  [1:0] in_1,
  output out_2,
  output out_3,
  output out_4,
  output out_5
);

  wire not_1_out, not_2_out, not_3_out, not_4_out;

  not not_1 (not_1_out, in_1[0]);
  not not_2 (not_2_out, in_1[1]);
  not not_3 (not_3_out, in_1[1]);
  not not_4 (not_4_out, in_1[0]);
  and and_1 (out_2, not_1_out, not_2_out);
  and and_2 (out_3, in_1[0], not_3_out);
  and and_3 (out_4, in_1[1], not_4_out);
  and and_4 (out_5, in_1[1], in_1[0]);
endmodule

module RAM (
  input  [1:0] CLOCK,
  input  [3:0] Entrada,
  input  [1:0] \Enderaçamento ,
  input  Limpar,
  output [3:0] Saida
);

  wire [1:0] undriven_2;
  wire [3:0] undriven;

  RAM_1x8 ram_1x8_1 (.Entrada(undriven), .in_3(undriven_2), .CLOCK(CLOCK), .Limpar(Limpar), .Saida(Saida));
endmodule

module Registrador_8_bit (
  input  [7:0] ENTRADA,
  input  Clock,
  output [7:0] SAIDA
);

  D_Flip_Flop d_ff_1 (.clk(Clock), .D(ENTRADA[7]), .Q(SAIDA[7]));  // open: Qn, preset, en, reset
  D_Flip_Flop d_ff_2 (.clk(Clock), .D(ENTRADA[6]), .Q(SAIDA[6]));  // open: Qn, preset, en, reset
  D_Flip_Flop d_ff_3 (.clk(Clock), .D(ENTRADA[5]), .Q(SAIDA[5]));  // open: Qn, preset, en, reset
  D_Flip_Flop d_ff_4 (.clk(Clock), .D(ENTRADA[4]), .Q(SAIDA[4]));  // open: Qn, preset, en, reset
  D_Flip_Flop d_ff_5 (.clk(Clock), .D(ENTRADA[3]), .Q(SAIDA[3]));  // open: Qn, preset, en, reset
  D_Flip_Flop d_ff_6 (.clk(Clock), .D(ENTRADA[2]), .Q(SAIDA[2]));  // open: Qn, preset, en, reset
  D_Flip_Flop d_ff_7 (.clk(Clock), .D(ENTRADA[1]), .Q(SAIDA[1]));  // open: Qn, preset, en, reset
  D_Flip_Flop d_ff_8 (.clk(Clock), .D(ENTRADA[0]), .Q(SAIDA[0]));  // open: Qn, preset, en, reset
endmodule

module Banco_de_Registrador (
  input  [7:0] Rx,
  input  [3:0] Rx_select,
  input  [7:0] Data_IN,
  input  [7:0] Ry,
  input  [3:0] Ry_select,
  input  Write,
  input  [3:0] Write_select
);

  wire demultiplexer_1_out0, demultiplexer_1_out1, demultiplexer_1_out2, demultiplexer_1_out3,
       demultiplexer_1_out4, demultiplexer_1_out5, demultiplexer_1_out6, demultiplexer_1_out7,
       demultiplexer_1_out8, demultiplexer_1_out9, demultiplexer_1_out11, demultiplexer_1_out12,
       demultiplexer_1_out13, demultiplexer_1_out14, demultiplexer_1_out15;
  wire [3:0] undriven, undriven_2;
  wire [7:0] multiplexer_1_out, multiplexer_2_out, register_1_q, register_2_q, register_3_q, register_4_q,
       register_5_q, register_6_q, register_7_q, register_8_q, register_9_q, register_10_q, register_11_q,
       register_12_q, register_13_q, register_14_q, register_15_q, register_16_q;

  Demultiplexer #(.select(4)) demultiplexer_1 (
    .out0(demultiplexer_1_out0), .out1(demultiplexer_1_out1), .out2(demultiplexer_1_out2),
    .out3(demultiplexer_1_out3), .out4(demultiplexer_1_out4), .out5(demultiplexer_1_out5),
    .out6(demultiplexer_1_out6), .out7(demultiplexer_1_out7), .out8(demultiplexer_1_out8),
    .out9(demultiplexer_1_out9), .out10(demultiplexer_1_out9), .out11(demultiplexer_1_out11),
    .out12(demultiplexer_1_out12), .out13(demultiplexer_1_out13), .out14(demultiplexer_1_out14),
    .out15(demultiplexer_1_out15), .in(Write), .sel(Write_select));  // open: en
  Register register_1 (.D(Data_IN), .en(demultiplexer_1_out0), .Q(register_1_q));  // open: clk, clr
  Register register_2 (.D(Data_IN), .en(demultiplexer_1_out1), .Q(register_2_q));  // open: clk, clr
  Register register_3 (.D(Data_IN), .en(demultiplexer_1_out2), .Q(register_3_q));  // open: clk, clr
  Register register_4 (.D(Data_IN), .en(demultiplexer_1_out3), .Q(register_4_q));  // open: clk, clr
  Register register_5 (.D(Data_IN), .en(demultiplexer_1_out4), .Q(register_5_q));  // open: clk, clr
  Register register_6 (.D(Data_IN), .en(demultiplexer_1_out5), .Q(register_6_q));  // open: clk, clr
  Register register_7 (.D(Data_IN), .en(demultiplexer_1_out6), .Q(register_7_q));  // open: clk, clr
  Register register_8 (.D(Data_IN), .en(demultiplexer_1_out7), .Q(register_8_q));  // open: clk, clr
  Register register_9 (.D(Data_IN), .en(demultiplexer_1_out8), .Q(register_9_q));  // open: clk, clr
  Register register_10 (.D(Data_IN), .en(demultiplexer_1_out9), .Q(register_10_q));  // open: clk, clr
  Register register_11 (.D(Data_IN), .en(demultiplexer_1_out9), .Q(register_11_q));  // open: clk, clr
  Register register_12 (.D(Data_IN), .en(demultiplexer_1_out11), .Q(register_12_q));  // open: clk, clr
  Register register_13 (.D(Data_IN), .en(demultiplexer_1_out12), .Q(register_13_q));  // open: clk, clr
  Register register_14 (.D(Data_IN), .en(demultiplexer_1_out13), .Q(register_14_q));  // open: clk, clr
  Register register_15 (.D(Data_IN), .en(demultiplexer_1_out14), .Q(register_15_q));  // open: clk, clr
  Register register_16 (.D(Data_IN), .en(demultiplexer_1_out15), .Q(register_16_q));  // open: clk, clr
  Multiplexer #(.select(4), .width(8)) multiplexer_1 (
    .in0(register_1_q), .in1(register_2_q), .in2(register_3_q), .in3(register_4_q), .in4(register_5_q),
    .in5(register_6_q), .in6(register_7_q), .in7(register_8_q), .in8(register_9_q), .in9(register_10_q),
    .in10(register_11_q), .in11(register_12_q), .in12(register_13_q), .in13(register_14_q),
    .in14(register_15_q), .in15(register_16_q), .out(multiplexer_1_out), .sel(undriven));  // open: en
  Multiplexer #(.select(4), .width(8)) multiplexer_2 (
    .in0(register_1_q), .in1(register_2_q), .in2(register_3_q), .in3(register_4_q), .in4(register_5_q),
    .in5(register_6_q), .in6(register_7_q), .in7(register_8_q), .in8(register_9_q), .in9(register_10_q),
    .in10(register_11_q), .in11(register_12_q), .in12(register_13_q), .in13(register_14_q),
    .in14(register_15_q), .in15(register_16_q), .out(multiplexer_2_out), .sel(undriven_2));  // open: en
endmodule

module Somador_8_bits (
  input  inteiro,
  input  in_2,
  input  in_3,
  input  in_4,
  input  in_5,
  input  in_6,
  input  in_7,
  input  in_8,
  input  in_9,
  input  in_10,
  input  in_11,
  input  in_12,
  input  in_13,
  input  in_14,
  input  in_15,
  input  in_16,
  input  in_17,
  input  overflow,
  input  in_19,
  input  in_20,
  input  in_21,
  input  in_22,
  input  in_23,
  input  in_24,
  input  in_25,
  input  in_26
);

  wire adder_2_cout, adder_3_cout, adder_4_cout, adder_5_cout, adder_6_cout, adder_7_cout, adder_8_cout;

  Adder #(.width(1)) adder_1 (.a(in_10), .b(in_2), .out(in_19), .cin(adder_2_cout), .cout(overflow));
  Adder #(.width(1)) adder_2 (.a(in_11), .b(in_3), .out(in_20), .cin(adder_3_cout), .cout(adder_2_cout));
  Adder #(.width(1)) adder_3 (.a(in_12), .b(in_4), .out(in_21), .cin(adder_4_cout), .cout(adder_3_cout));
  Adder #(.width(1)) adder_4 (.a(in_13), .b(in_5), .out(in_22), .cin(adder_5_cout), .cout(adder_4_cout));
  Adder #(.width(1)) adder_5 (.a(in_14), .b(in_6), .out(in_23), .cin(adder_6_cout), .cout(adder_5_cout));
  Adder #(.width(1)) adder_6 (.a(in_15), .b(in_7), .out(in_24), .cin(adder_7_cout), .cout(adder_6_cout));
  Adder #(.width(1)) adder_7 (.a(in_16), .b(in_8), .out(in_25), .cin(adder_8_cout), .cout(adder_7_cout));
  Adder #(.width(1)) adder_8 (.a(in_17), .b(in_9), .out(in_26), .cin(inteiro), .cout(adder_8_cout));
endmodule

// ROM
module ROM_vlr (
  input  [7:0] Entrada,
  input  Clock,
  input  Set,
  input  Reset,
  output [7:0] \Saída 
);

  D_Flip_Flop d_ff_1 (.clk(Clock), .D(Entrada[7]), .Q(\Saída [0]), .preset(Set), .reset(Reset));  // open: Qn, en
  D_Flip_Flop d_ff_2 (.clk(Clock), .D(Entrada[6]), .Q(\Saída [1]), .preset(Set), .reset(Reset));  // open: Qn, en
  D_Flip_Flop d_ff_3 (.clk(Clock), .D(Entrada[5]), .Q(\Saída [2]), .preset(Set), .reset(Reset));  // open: Qn, en
  D_Flip_Flop d_ff_4 (.clk(Clock), .D(Entrada[4]), .Q(\Saída [3]), .preset(Set), .reset(Reset));  // open: Qn, en
  D_Flip_Flop d_ff_5 (.clk(Clock), .D(Entrada[3]), .Q(\Saída [4]), .preset(Set), .reset(Reset));  // open: Qn, en
  D_Flip_Flop d_ff_6 (.clk(Clock), .D(Entrada[2]), .Q(\Saída [5]), .preset(Set), .reset(Reset));  // open: Qn, en
  D_Flip_Flop d_ff_7 (.clk(Clock), .D(Entrada[1]), .Q(\Saída [6]), .preset(Set), .reset(Reset));  // open: Qn, en
  D_Flip_Flop d_ff_8 (.clk(Clock), .D(Entrada[0]), .Q(\Saída [7]), .preset(Set), .reset(Reset));  // open: Qn, en
endmodule

module ROM (
  input  _1___ler,
  input  [7:0] Entrada,
  input  set,
  input  reset,
  output [3:0] out_5,
  output [7:0] out_6,
  output [7:0] out_7,
  output [7:0] out_8,
  output [7:0] out_9,
  output [7:0] out_10,
  output [7:0] out_11,
  output [7:0] out_12,
  output [7:0] out_13,
  output [7:0] out_14,
  output [7:0] out_15,
  output [7:0] out_16,
  output [7:0] out_17,
  output [7:0] out_18,
  output [7:0] out_19,
  output [7:0] out_20,
  output [7:0] out_21,
  output [7:0] out_22
);

  wire Clock_out, demultiplexer_1_out0, demultiplexer_1_out1, demultiplexer_1_out2, demultiplexer_1_out3,
       demultiplexer_1_out4, demultiplexer_1_out5, demultiplexer_1_out6, demultiplexer_1_out7,
       demultiplexer_1_out8, demultiplexer_1_out9, demultiplexer_1_out10, demultiplexer_1_out11,
       demultiplexer_1_out12, demultiplexer_1_out13, demultiplexer_1_out14, demultiplexer_1_out15,
       multiplexer_1_out;
  wire [3:0] counter_1_q;
  wire [7:0] multiplexer_2_out;

  Clock Clock (.out(Clock_out));
  Multiplexer multiplexer_1 (.in0(Clock_out), .in1(1'b0), .out(multiplexer_1_out), .sel(_1___ler));  // open: en
  Counter #(.width(4), .max('hf)) counter_1 (
    .count(1'b1), .Q(counter_1_q), .clk(multiplexer_1_out));  // open: load, D, carry, clr
  Demultiplexer #(.select(4)) demultiplexer_1 (
    .out0(demultiplexer_1_out0), .out1(demultiplexer_1_out1), .out2(demultiplexer_1_out2),
    .out3(demultiplexer_1_out3), .out4(demultiplexer_1_out4), .out5(demultiplexer_1_out5),
    .out6(demultiplexer_1_out6), .out7(demultiplexer_1_out7), .out8(demultiplexer_1_out8),
    .out9(demultiplexer_1_out9), .out10(demultiplexer_1_out10), .out11(demultiplexer_1_out11),
    .out12(demultiplexer_1_out12), .out13(demultiplexer_1_out13), .out14(demultiplexer_1_out14),
    .out15(demultiplexer_1_out15), .in(1'b1), .sel(counter_1_q));  // open: en
  Subtractor #(.width(4)) subtractor_1 (.a(counter_1_q), .b(4'b0001), .out(out_5));  // open: bin, bout
  ROM_vlr rom_vlr_1 (.Entrada(Entrada), .Clock(demultiplexer_1_out0), .Set(set), .Reset(reset), .\Saída (out_6));
  ROM_vlr rom_vlr_2 (.Entrada(Entrada), .Clock(demultiplexer_1_out1), .Set(set), .Reset(reset), .\Saída (out_7));
  ROM_vlr rom_vlr_3 (.Entrada(Entrada), .Clock(demultiplexer_1_out2), .Set(set), .Reset(reset), .\Saída (out_8));
  ROM_vlr rom_vlr_4 (.Entrada(Entrada), .Clock(demultiplexer_1_out3), .Set(set), .Reset(reset), .\Saída (out_9));
  ROM_vlr rom_vlr_5 (.Entrada(Entrada), .Clock(demultiplexer_1_out4), .Set(set), .Reset(reset), .\Saída (out_10));
  ROM_vlr rom_vlr_6 (.Entrada(Entrada), .Clock(demultiplexer_1_out5), .Set(set), .Reset(reset), .\Saída (out_11));
  ROM_vlr rom_vlr_7 (.Entrada(Entrada), .Clock(demultiplexer_1_out6), .Set(set), .Reset(reset), .\Saída (out_12));
  ROM_vlr rom_vlr_8 (.Entrada(Entrada), .Clock(demultiplexer_1_out7), .Set(set), .Reset(reset), .\Saída (out_14));
  ROM_vlr rom_vlr_9 (.Entrada(Entrada), .Clock(demultiplexer_1_out8), .Set(set), .Reset(reset), .\Saída (out_15));
  ROM_vlr rom_vlr_10 (.Entrada(Entrada), .Clock(demultiplexer_1_out9), .Set(set), .Reset(reset), .\Saída (out_16));
  ROM_vlr rom_vlr_11 (.Entrada(Entrada), .Clock(demultiplexer_1_out10), .Set(set), .Reset(reset), .\Saída (out_17));
  ROM_vlr rom_vlr_12 (.Entrada(Entrada), .Clock(demultiplexer_1_out11), .Set(set), .Reset(reset), .\Saída (out_18));
  ROM_vlr rom_vlr_13 (.Entrada(Entrada), .Clock(demultiplexer_1_out12), .Set(set), .Reset(reset), .\Saída (out_19));
  ROM_vlr rom_vlr_14 (.Entrada(Entrada), .Clock(demultiplexer_1_out13), .Set(set), .Reset(reset), .\Saída (out_20));
  ROM_vlr rom_vlr_15 (.Entrada(Entrada), .Clock(demultiplexer_1_out14), .Set(set), .Reset(reset), .\Saída (out_21));
  ROM_vlr rom_vlr_16 (.Entrada(Entrada), .Clock(demultiplexer_1_out15), .Set(set), .Reset(reset), .\Saída (out_22));
  Multiplexer #(.select(4), .width(8)) multiplexer_2 (
    .in0(out_6), .in1(out_7), .in2(out_8), .in3(out_9), .in4(out_10), .in5(out_11), .in6(out_12),
    .in7(out_14), .in8(out_15), .in9(out_16), .in10(out_17), .in11(out_18), .in12(out_19), .in13(out_20),
    .in14(out_21), .in15(out_22), .out(multiplexer_2_out), .sel(out_5));  // open: en
  Multiplexer #(.width(8)) multiplexer_3 (
    .in0({8{1'b0}}), .in1(multiplexer_2_out), .out(out_13), .sel(_1___ler));  // open: en
endmodule

// ULA CTRL
module ULA_ctrl (
  input  [1:0] A_B,
  input  [1:0] SA_SB,
  input  Cin,
  input  [2:0] Seletor,
  input  CinShiftE,
  input  CinShiftD,
  output S,
  output Cout,
  output CoutShift_E,
  output CoutShift_D
);

  wire _0_2_out, _000_out, _0_out, _1_2_out, _001_out, _1_out, _010_out, _011_2_out, _011_out, _100_2_out,
       _100_out, _101_out, _110_out, adder_1_cout, adder_1_out, and_1_out, not_1_out, not_2_out, not_3_out,
       not_4_out, not_5_out, not_6_out, not_7_out, not_8_out, not_9_out, not_10_out, not_11_out, not_12_out,
       not_13_out, not_14_out, not_15_out, not_16_out, not_17_out, not_18_out, not_19_out, not_20_out,
       not_21_out, or_1_out, or_2_out, or_3_out, subtractor_1_bout, subtractor_1_out, xor_1_out;

  // Probe on A_B[1]
  // Probe on A_B[0]
  not not_1 (not_1_out, SA_SB[1]);
  not not_2 (not_2_out, A_B[1]);
  not not_3 (not_3_out, SA_SB[0]);
  not not_4 (not_4_out, A_B[0]);
  and _0 (_0_out, not_1_out, A_B[1]);
  and _1 (_1_out, SA_SB[1], not_2_out);
  and _0_2 (_0_2_out, not_3_out, A_B[0]);
  and _1_2 (_1_2_out, SA_SB[0], not_4_out);
  or or_1 (or_1_out, _0_out, _1_out);
  or or_2 (or_2_out, _0_2_out, _1_2_out);
  and and_1 (and_1_out, or_1_out, or_2_out);
  or or_3 (or_3_out, or_1_out, or_2_out);
  xor xor_1 (xor_1_out, or_1_out, or_2_out);
  Adder #(.width(1)) adder_1 (.a(or_1_out), .b(or_2_out), .out(adder_1_out), .cin(Cin), .cout(adder_1_cout));
  Subtractor #(.width(1)) subtractor_1 (
    .a(or_1_out), .b(or_2_out), .out(subtractor_1_out), .bin(Cin), .bout(subtractor_1_bout));
  not not_5 (not_5_out, Seletor[0]);
  not not_6 (not_6_out, Seletor[1]);
  not not_7 (not_7_out, Seletor[2]);
  not not_8 (not_8_out, Seletor[1]);
  not not_9 (not_9_out, Seletor[2]);
  not not_10 (not_10_out, Seletor[0]);
  not not_11 (not_11_out, Seletor[2]);
  not not_12 (not_12_out, Seletor[2]);
  not not_13 (not_13_out, Seletor[2]);
  not not_14 (not_14_out, Seletor[0]);
  not not_15 (not_15_out, Seletor[1]);
  not not_16 (not_16_out, Seletor[0]);
  not not_17 (not_17_out, Seletor[1]);
  not not_18 (not_18_out, Seletor[1]);
  not not_19 (not_19_out, Seletor[1]);
  not not_20 (not_20_out, Seletor[0]);
  not not_21 (not_21_out, Seletor[0]);
  and _000 (_000_out, not_5_out, not_6_out, not_7_out, and_1_out);
  and _001 (_001_out, Seletor[0], not_8_out, not_9_out, or_3_out);
  and _010 (_010_out, not_10_out, Seletor[1], not_11_out, xor_1_out);
  and _011 (_011_out, Seletor[0], Seletor[1], not_12_out, adder_1_out);
  and _011_2 (_011_2_out, Seletor[0], Seletor[1], not_13_out, adder_1_cout);
  and _100 (_100_out, not_14_out, not_15_out, Seletor[2], subtractor_1_out);
  and _100_2 (_100_2_out, not_16_out, not_17_out, Seletor[2], subtractor_1_bout);
  and _101 (_101_out, Seletor[0], not_18_out, Seletor[2], CinShiftE);
  and _101_2 (CoutShift_E, Seletor[0], not_19_out, Seletor[2], A_B[1]);
  and _110 (_110_out, not_20_out, Seletor[1], Seletor[2], CinShiftD);
  and _110_2 (CoutShift_D, not_21_out, Seletor[1], Seletor[2], A_B[1]);
  or or_4 (S, _000_out, _001_out, _010_out, _011_out, _100_out, _101_out, _110_out);
  or or_5 (Cout, _011_2_out, _100_2_out);
endmodule

module ULA_main (
  input  [4:0] Seletor,
  input  [7:0] A,
  input  [7:0] S,
  input  [7:0] B,
  output Overflow
);

  wire ula_ctrl_1_cout, ula_ctrl_1_coutshift_e, ula_ctrl_2_cout, ula_ctrl_2_coutshift_e, ula_ctrl_3_cout,
       ula_ctrl_3_coutshift_d, ula_ctrl_3_coutshift_e, ula_ctrl_4_cout, ula_ctrl_4_coutshift_d,
       ula_ctrl_4_coutshift_e, ula_ctrl_5_cout, ula_ctrl_5_coutshift_d, ula_ctrl_5_coutshift_e,
       ula_ctrl_6_cout, ula_ctrl_6_coutshift_d, ula_ctrl_6_coutshift_e, ula_ctrl_7_cout,
       ula_ctrl_7_coutshift_d, ula_ctrl_8_coutshift_d;

  ULA_ctrl ula_ctrl_1 (
    .CinShiftE(1'b0), .CinShiftD(ula_ctrl_3_coutshift_d), .S(S[0]), .Cout(ula_ctrl_1_cout),
    .CoutShift_E(ula_ctrl_1_coutshift_e), .A_B({B[0], A[7]}), .SA_SB(Seletor[4:3]), .Cin(1'b0),
    .Seletor(Seletor[2:0]));  // open: CoutShift_D
  ULA_ctrl ula_ctrl_2 (
    .CinShiftE(1'b0), .CinShiftD(ula_ctrl_4_coutshift_d), .S(S[1]), .Cout(ula_ctrl_2_cout),
    .CoutShift_E(ula_ctrl_2_coutshift_e), .A_B({B[1], A[6]}), .SA_SB(Seletor[4:3]), .Cin(ula_ctrl_1_cout),
    .Seletor(Seletor[2:0]));  // open: CoutShift_D
  ULA_ctrl ula_ctrl_3 (
    .CinShiftE(ula_ctrl_1_coutshift_e), .CinShiftD(ula_ctrl_5_coutshift_d), .S(S[2]), .Cout(ula_ctrl_3_cout),
    .CoutShift_E(ula_ctrl_3_coutshift_e), .CoutShift_D(ula_ctrl_3_coutshift_d), .A_B({B[2], A[5]}),
    .SA_SB(Seletor[4:3]), .Cin(ula_ctrl_2_cout), .Seletor(Seletor[2:0]));
  ULA_ctrl ula_ctrl_4 (
    .CinShiftE(ula_ctrl_2_coutshift_e), .CinShiftD(ula_ctrl_6_coutshift_d), .S(S[3]), .Cout(ula_ctrl_4_cout),
    .CoutShift_E(ula_ctrl_4_coutshift_e), .CoutShift_D(ula_ctrl_4_coutshift_d), .A_B({B[3], A[4]}),
    .SA_SB(Seletor[4:3]), .Cin(ula_ctrl_3_cout), .Seletor(Seletor[2:0]));
  ULA_ctrl ula_ctrl_5 (
    .CinShiftE(ula_ctrl_3_coutshift_e), .CinShiftD(ula_ctrl_7_coutshift_d), .S(S[4]), .Cout(ula_ctrl_5_cout),
    .CoutShift_E(ula_ctrl_5_coutshift_e), .CoutShift_D(ula_ctrl_5_coutshift_d), .A_B({B[4], A[3]}),
    .SA_SB(Seletor[4:3]), .Cin(ula_ctrl_4_cout), .Seletor(Seletor[2:0]));
  ULA_ctrl ula_ctrl_6 (
    .CinShiftE(ula_ctrl_4_coutshift_e), .CinShiftD(ula_ctrl_8_coutshift_d), .S(S[5]), .Cout(ula_ctrl_6_cout),
    .CoutShift_E(ula_ctrl_6_coutshift_e), .CoutShift_D(ula_ctrl_6_coutshift_d), .A_B({B[5], A[2]}),
    .SA_SB(Seletor[4:3]), .Cin(ula_ctrl_5_cout), .Seletor(Seletor[2:0]));
  ULA_ctrl ula_ctrl_7 (
    .CinShiftE(ula_ctrl_5_coutshift_e), .CinShiftD(1'b0), .S(S[6]), .Cout(ula_ctrl_7_cout),
    .CoutShift_D(ula_ctrl_7_coutshift_d), .A_B({B[6], A[1]}), .SA_SB(Seletor[4:3]), .Cin(ula_ctrl_6_cout),
    .Seletor(Seletor[2:0]));  // open: CoutShift_E
  ULA_ctrl ula_ctrl_8 (
    .CinShiftE(ula_ctrl_6_coutshift_e), .CinShiftD(1'b0), .S(S[7]), .Cout(Overflow),
    .CoutShift_D(ula_ctrl_8_coutshift_d), .A_B({B[7], A[0]}), .SA_SB(Seletor[4:3]), .Cin(ula_ctrl_7_cout),
    .Seletor(Seletor[2:0]));  // open: CoutShift_E
endmodule

module FF_JK (
  input  SET,
  input  J,
  input  CLOCK,
  input  K,
  input  RESET,
  output Q,
  output nQ
);

  wire nand_1_out, nand_2_out, nand_3_out, nand_4_out, nand_5_out, nand_6_out, not_1_out, not_2_out,
       not_3_out, not_4_out;

  not not_1 (not_1_out, CLOCK);
  not not_2 (not_2_out, SET);
  not not_3 (not_3_out, RESET);
  nand nand_1 (nand_1_out, nQ, J, not_1_out);
  nand nand_2 (nand_2_out, not_1_out, K, Q);
  nand nand_3 (nand_3_out, not_2_out, nand_1_out, nand_4_out);
  not not_4 (not_4_out, not_1_out);
  nand nand_4 (nand_4_out, nand_3_out, nand_2_out, not_3_out);
  nand nand_5 (nand_5_out, nand_3_out, not_3_out, not_4_out);
  nand nand_6 (nand_6_out, not_4_out, not_2_out, nand_4_out);
  nand nand_7 (Q, not_2_out, nQ, nand_5_out);
  nand nand_8 (nQ, nand_6_out, Q, not_3_out);
endmodule

module Ctrl_mips_16_bits (
  input  [5:0] in_1,
  input  in_2,
  input  in_3,
  output RegDST,
  output OrigALU,
  output MemParaReg,
  output EscReg,
  output LeMem,
  output EscMem,
  output AluOp1,
  output AluOp0,
  output RESET,
  output AtualPC
);

  wire and_1_out, and_2_out, clock_1_out, demultiplexer_1_out2, demultiplexer_2_out1, demultiplexer_2_out5,
       demultiplexer_3_out1, demultiplexer_3_out3, ff_jk_1_q, LW_out, not_1_out, not_2_out, not_3_out,
       not_4_out, not_5_out, not_6_out, not_7_out, not_8_out, not_9_out, not_10_out, not_11_out, ON_OFF_out,
       or_1_out, or_2_out, R_out, SW_out;
  wire [2:0] counter_1_q;

  not not_1 (not_1_out, in_1[0]);
  not not_2 (not_2_out, in_1[1]);
  not not_3 (not_3_out, in_1[2]);
  not not_4 (not_4_out, in_1[3]);
  not not_5 (not_5_out, in_1[4]);
  not not_6 (not_6_out, in_1[5]);
  not not_7 (not_7_out, in_1[1]);
  not not_8 (not_8_out, in_1[2]);
  not not_9 (not_9_out, in_1[3]);
  not not_10 (not_10_out, in_1[1]);
  not not_11 (not_11_out, in_1[3]);
  Button ON_OFF (.out(ON_OFF_out));
  and R (R_out, not_1_out, not_2_out, not_3_out, not_4_out, not_5_out, not_6_out);
  and LW (LW_out, in_1[0], not_7_out, not_8_out, not_9_out, in_1[4], in_1[5]);
  and SW (SW_out, in_1[0], not_10_out, in_1[2], not_11_out, in_1[4], in_1[5]);
  and and_1 (and_1_out, in_1[0], in_1[1], in_1[2], in_1[3], in_1[4], in_1[5]);
  or or_1 (or_1_out, R_out, LW_out, SW_out);
  or or_2 (or_2_out, and_1_out, ON_OFF_out);
  Clock clock_1 (.out(clock_1_out));
  FF_JK ff_jk_1 (.J(1'b1), .K(1'b1), .Q(ff_jk_1_q), .SET(in_2), .RESET(in_3), .CLOCK(or_2_out));  // open: nQ
  not not_12 (RESET, ff_jk_1_q);
  and and_2 (and_2_out, clock_1_out, ff_jk_1_q);
  Counter #(.width(3), .max('h7)) counter_1 (
    .count(or_1_out), .Q(counter_1_q), .clk(and_2_out), .clr(RESET));  // open: load, D, carry
  Demultiplexer #(.select(3)) demultiplexer_1 (
    .out1(RegDST), .out2(demultiplexer_1_out2), .out3(AluOp1), .out4(EscReg), .in(R_out), .sel(counter_1_q));  // open: out0, out5, out6, out7, en
  Demultiplexer #(.select(3)) demultiplexer_2 (
    .out1(demultiplexer_2_out1), .out2(LeMem), .out3(MemParaReg), .out4(EscReg), .out5(demultiplexer_2_out5),
    .in(LW_out), .sel(counter_1_q));  // open: out0, out6, out7, en
  Demultiplexer #(.select(3)) demultiplexer_3 (
    .out1(demultiplexer_3_out1), .out2(EscMem), .out3(demultiplexer_3_out3), .in(SW_out), .sel(counter_1_q));  // open: out0, out4, out5, out6, out7, en
  or or_3 (AtualPC, EscReg, demultiplexer_2_out5, demultiplexer_3_out3);
  or or_4 (OrigALU, demultiplexer_1_out2, demultiplexer_2_out1, demultiplexer_3_out1);

  assign AluOp0 = 1'b0;
endmodule

module Extensor (
  input  [3:0] Input,
  input  \Extensão_tipo ,
  output [7:0] Sinal_final
);


  assign Sinal_final = {{4{\Extensão_tipo }}, Input};
endmodule

module FF_D (
  input  SET,
  input  Input,
  input  CLOCK,
  input  RESET,
  output Q,
  output nQ
);

  wire nand_1_out, nand_2_out, nand_3_out, nand_4_out, nand_5_out, nand_6_out, not_1_out, not_2_out,
       not_3_out, not_4_out;

  not not_1 (not_1_out, Input);
  not not_2 (not_2_out, SET);
  not not_3 (not_3_out, RESET);
  nand nand_1 (nand_1_out, nQ, Input, CLOCK);
  nand nand_2 (nand_2_out, CLOCK, not_1_out, Q);
  nand nand_3 (nand_3_out, not_2_out, nand_1_out, nand_4_out);
  not not_4 (not_4_out, CLOCK);
  nand nand_4 (nand_4_out, nand_3_out, nand_2_out, not_3_out);
  nand nand_5 (nand_5_out, nand_3_out, not_3_out, not_4_out);
  nand nand_6 (nand_6_out, not_4_out, not_2_out, nand_4_out);
  nand nand_7 (Q, not_2_out, nQ, nand_5_out);
  nand nand_8 (nQ, nand_6_out, Q, not_3_out);
endmodule

module MaquinaEstados (
  input  SET,
  input  RESET,
  input  P,
  output R
);

  wire and_1_out, and_2_out, and_3_out, and_4_out, and_5_out, and_6_out, and_7_out, and_8_out, and_9_out,
       clock_1_out, ff_d_1_q, ff_d_2_q, ff_d_3_q, not_1_out, not_2_out, not_3_out, not_4_out, not_5_out,
       not_6_out, not_7_out, or_1_out, or_2_out, or_3_out;

  Clock clock_1 (.out(clock_1_out));
  and and_1 (and_1_out, not_5_out, R);
  and and_2 (and_2_out, not_5_out, ff_d_1_q);
  and and_3 (and_3_out, not_1_out, not_2_out, not_3_out, not_4_out);
  not not_1 (not_1_out, R);
  not not_2 (not_2_out, ff_d_3_q);
  not not_3 (not_3_out, ff_d_2_q);
  not not_4 (not_4_out, ff_d_1_q);
  or or_1 (or_1_out, and_3_out, and_2_out, and_1_out);
  LED A (.in(ff_d_1_q));
  LED B (.in(ff_d_2_q));
  not not_5 (not_5_out, P);
  FF_D ff_d_1 (.Input(or_1_out), .CLOCK(clock_1_out), .SET(SET), .RESET(RESET), .Q(ff_d_1_q));  // open: nQ
  LED D (.in(R));
  LED C (.in(ff_d_3_q));
  and and_4 (and_4_out, P, ff_d_1_q);
  and and_5 (and_5_out, P, R);
  and and_6 (and_6_out, not_6_out, ff_d_2_q);
  or or_2 (or_2_out, and_6_out, and_5_out, and_4_out);
  not not_6 (not_6_out, P);
  FF_D ff_d_2 (.Input(or_2_out), .CLOCK(clock_1_out), .SET(SET), .RESET(RESET), .Q(ff_d_2_q));  // open: nQ
  and and_7 (and_7_out, P, ff_d_2_q);
  and and_8 (and_8_out, not_7_out, ff_d_3_q);
  or or_3 (or_3_out, and_8_out, and_7_out);
  not not_7 (not_7_out, P);
  FF_D ff_d_3 (.Input(or_3_out), .CLOCK(clock_1_out), .SET(SET), .RESET(RESET), .Q(ff_d_3_q));  // open: nQ
  and and_9 (and_9_out, P, ff_d_3_q);
  FF_D ff_d_4 (.Input(and_9_out), .CLOCK(clock_1_out), .SET(SET), .RESET(RESET), .Q(R));  // open: nQ
endmodule

module FF_T (
  input  SET,
  input  T,
  input  CLOCK,
  input  RESET,
  output Q,
  output nQ
);

  wire nand_1_out, nand_2_out, nand_3_out, nand_4_out, nand_5_out, nand_6_out, not_1_out, not_2_out,
       not_3_out, not_4_out;

  not not_1 (not_1_out, CLOCK);
  not not_2 (not_2_out, SET);
  not not_3 (not_3_out, RESET);
  nand nand_1 (nand_1_out, nQ, T, not_1_out);
  nand nand_2 (nand_2_out, not_1_out, T, Q);
  nand nand_3 (nand_3_out, not_2_out, nand_1_out, nand_4_out);
  not not_4 (not_4_out, not_1_out);
  nand nand_4 (nand_4_out, nand_3_out, nand_2_out, not_3_out);
  nand nand_5 (nand_5_out, nand_3_out, not_3_out, not_4_out);
  nand nand_6 (nand_6_out, not_4_out, not_2_out, nand_4_out);
  nand nand_7 (Q, not_2_out, nQ, nand_5_out);
  nand nand_8 (nQ, nand_6_out, Q, not_3_out);
endmodule

module Contador (
  input  SET,
  input  RESET,
  output out_3,
  output out_4,
  output out_5,
  output out_6
);

  wire and_1_out, and_2_out, clock_1_out;

  Clock clock_1 (.out(clock_1_out));
  and and_1 (and_1_out, and_2_out, out_4);
  FF_T ff_t_1 (.T(and_1_out), .CLOCK(clock_1_out), .Q(out_3), .SET(SET), .RESET(RESET));  // open: nQ
  and and_2 (and_2_out, out_6, out_5);
  FF_T ff_t_2 (.T(and_2_out), .CLOCK(clock_1_out), .Q(out_4), .SET(SET), .RESET(RESET));  // open: nQ
  FF_T ff_t_3 (.T(out_6), .CLOCK(clock_1_out), .Q(out_5), .SET(SET), .RESET(RESET));  // open: nQ
  FF_T ff_t_4 (.T(1'b1), .CLOCK(clock_1_out), .Q(out_6), .SET(SET), .RESET(RESET));  // open: nQ
endmodule
