// Logisim project relatorio.circ as structural Verilog: 13 circuits, main circuit Flip Flop D e JK
module Flip_Flop_D_e_JK (
  input  Clock,
  input  D,
  input  Preset,
  input  Clear,
  input  Enable,
  input  J,
  input  Clock_2,
  input  K,
  input  Preset_2,
  input  Enable_2,
  input  Clear_2,
  output \Saída ,
  output Complemento,
  output \Saída_2 ,
  output Complemento_2
);

  D_Flip_Flop d_ff_1 (.clk(Clock), .D(D), .Q(\Saída ), .Qn(Complemento), .preset(Preset), .en(Enable), .reset(Clear));
  J_K_Flip_Flop j_k_ff_1 (
    .J(J), .clk(Clock_2), .K(K), .Q(\Saída_2 ), .Qn(Complemento_2), .preset(Preset_2), .en(Enable_2),
    .reset(Clear_2));
endmodule

module Multiplexador (
  input  _0,
  input  _1,
  input  _2,
  input  _3,
  input  [1:0] select,
  output \saída ,
  output complemento
);

  Multiplexer #(.select(2)) multiplexer_1 (
    .in0(_0), .in1(_1), .in2(_2), .in3(_3), .out(\saída ), .sel(select), .en(complemento));
endmodule

module XOR (
  input  J,
  input  K,
  output out_3
);

  wire and_0_out, and_1_out, not_1_out, not_2_out;

  not not_1 (not_1_out, J);
  not not_2 (not_2_out, K);
  and and_0 (and_0_out, not_1_out, K);
  and and_1 (and_1_out, J, not_2_out);
  or \or  (out_3, and_0_out, and_1_out);
endmodule

module Somador_8_bits_com_4 (
  input  inteiro,
  input  in_2,
  input  in_3,
  input  in_4,
  input  in_5,
  input  in_6,
  input  in_7,
  input  in_8,
  input  in_9,
  input  in_10,
  input  in_11,
  input  in_12,
  input  in_13,
  input  in_14,
  input  in_15,
  input  in_16,
  input  in_17,
  input  overflow
);

  wire adder_2_cout, adder_3_cout, adder_4_cout, adder_5_cout, adder_6_cout, adder_7_cout, adder_8_cout;
  wire [3:0] adder_4_out, adder_8_out;

  Adder #(.width(1)) adder_1 (.a(in_10), .b(in_2), .out(adder_4_out[3]), .cin(adder_2_cout), .cout(overflow));
  Adder #(.width(1)) adder_2 (.a(in_11), .b(in_3), .out(adder_4_out[2]), .cin(adder_3_cout), .cout(adder_2_cout));
  Hex_Digit_Display hex_digit_display_1 (.value(adder_4_out));  // open: dp
  Adder #(.width(1)) adder_3 (.a(in_12), .b(in_4), .out(adder_4_out[1]), .cin(adder_4_cout), .cout(adder_3_cout));
  Adder #(.width(1)) adder_4 (.a(in_13), .b(in_5), .out(adder_4_out[0]), .cin(adder_5_cout), .cout(adder_4_cout));
  Adder #(.width(1)) adder_5 (.a(in_14), .b(in_6), .out(adder_8_out[3]), .cin(adder_6_cout), .cout(adder_5_cout));
  Adder #(.width(1)) adder_6 (.a(in_15), .b(in_7), .out(adder_8_out[2]), .cin(adder_7_cout), .cout(adder_6_cout));
  Hex_Digit_Display hex_digit_display_2 (.value(adder_8_out));  // open: dp
  Adder #(.width(1)) adder_7 (.a(in_16), .b(in_8), .out(adder_8_out[1]), .cin(adder_8_cout), .cout(adder_7_cout));
  Adder #(.width(1)) adder_8 (.a(in_17), .b(in_9), .out(adder_8_out[0]), .cin(inteiro), .cout(adder_8_cout));
endmodule

module RAM_1x8 (
  input  [1:0] CLOCK,
  input  [3:0] Entrada,
  input  [1:0] in_3,
  input  Limpar,
  output [3:0] Saida
);

  wire chave_1_out_2, chave_1_out_3, chave_1_out_4, chave_1_out_5;
  wire [3:0] ram_1x4_1_p4, ram_1x4_2_saida, ram_1x4_3_saida, ram_1x4_4_p4;

  Chave chave_1 (
    .in_1(in_3), .out_2(chave_1_out_2), .out_3(chave_1_out_3), .out_4(chave_1_out_4), .out_5(chave_1_out_5));
  // RAM_1x4 ram_1x4_1: pin names not known; wires that end beside it: Entrada, CLOCK, chave_1_out_2, ram_1x4_1_p4, Limpar
  RAM_1x4 ram_1x4_2 (.Entrada(Entrada), .clock(CLOCK), .Ligar(chave_1_out_4), .Limpar(Limpar), .Saida(ram_1x4_2_saida));
  RAM_1x4 ram_1x4_3 (.Entrada(Entrada), .clock(CLOCK), .Ligar(chave_1_out_3), .Limpar(Limpar), .Saida(ram_1x4_3_saida));
  // RAM_1x4 ram_1x4_4: pin names not known; wires that end beside it: Entrada, CLOCK, chave_1_out_5, ram_1x4_4_p4, Limpar
  assign Saida = ram_1x4_3_saida | ram_1x4_1_p4 | ram_1x4_2_saida | ram_1x4_4_p4;  // OR_Gate or_1, 4 bits wide
endmodule

module RAM_1x4 (
  input  [1:0] clock,
  input  [3:0] Entrada,
  input  Ligar,
  input  Limpar,
  output [3:0] Saida
);

  RAM_1x2 ram_1x2_1 (.CLK(Entrada[0]), .in_1(clock), .Ligar(Ligar), .Limpar(Limpar), .out_5(Saida[1:0]));
  RAM_1x2 ram_1x2_2 (.CLK(Entrada[2]), .in_1(clock), .Ligar(Ligar), .Limpar(Limpar), .out_5(Saida[3:2]));
endmodule

module RAM_1x2 (
  input  [1:0] in_1,
  input  CLK,
  input  Ligar,
  input  Limpar,
  output [1:0] out_5
);

  wire j_k_ff_1_q, j_k_ff_2_q, not_1_out, not_2_out;

  not not_1 (not_1_out, in_1[1]);
  J_K_Flip_Flop j_k_ff_1 (
    .J(in_1[1]), .clk(CLK), .K(not_1_out), .Q(j_k_ff_1_q), .en(Ligar), .reset(Limpar));  // open: Qn, preset
  J_K_Flip_Flop j_k_ff_2 (
    .J(in_1[0]), .clk(CLK), .K(not_2_out), .Q(j_k_ff_2_q), .en(Ligar), .reset(Limpar));  // open: Qn, preset
  not not_2 (not_2_out, in_1[0]);
  and and_1 (out_5[0], Ligar, j_k_ff_2_q);
  and and_2 (out_5[1], Ligar, j_k_ff_1_q);
endmodule

module Chave (
  input  [1:0] in_1,
  output out_2,
  output out_3,
  output out_4,
  output out_5
);

  wire not_1_out, not_2_out, not_3_out, not_4_out;

  not not_1 (not_1_out, in_1[0]);
  not not_2 (not_2_out, in_1[1]);
  not not_3 (not_3_out, in_1[1]);
  not not_4 (not_4_out, in_1[0]);
  and and_1 (out_2, not_1_out, not_2_out);
  and and_2 (out_3, in_1[0], not_3_out);
  and and_3 (out_4, in_1[1], not_4_out);
  and and_4 (out_5, in_1[1], in_1[0]);
endmodule

module RAM (
  input  [1:0] CLOCK,
  input  [3:0] Entrada,
  input  [1:0] \Enderaçamento ,
  input  Limpar,
  output [3:0] Saida
);

  wire [1:0] undriven_2;
  wire [3:0] undriven;

  RAM_1x8 ram_1x8_1 (.Entrada(undriven), .in_3(undriven_2), .CLOCK(CLOCK), .Limpar(Limpar), .Saida(Saida));
endmodule

module Registrador_8_bit (
  input  [7:0] ENTRADA,
  input  Clock,
  output [7:0] SAIDA
);

  D_Flip_Flop d_ff_1 (.clk(Clock), .D(ENTRADA[7]), .Q(SAIDA[7]));  // open: Qn, preset, en, reset
  D_Flip_Flop d_ff_2 (.clk(Clock), .D(ENTRADA[6]), .Q(SAIDA[6]));  // open: Qn, preset, en, reset
  D_Flip_Flop d_ff_3 (.clk(Clock), .D(ENTRADA[5]), .Q(SAIDA[5]));  // open: Qn, preset, en, reset
  D_Flip_Flop d_ff_4 (.clk(Clock), .D(ENTRADA[4]), .Q(SAIDA[4]));  // open: Qn, preset, en, reset
  D_Flip_Flop d_ff_5 (.clk(Clock), .D(ENTRADA[3]), .Q(SAIDA[3]));  // open: Qn, preset, en, reset
  D_Flip_Flop d_ff_6 (.clk(Clock), .D(ENTRADA[2]), .Q(SAIDA[2]));  // open: Qn, preset, en, reset
  D_Flip_Flop d_ff_7 (.clk(Clock), .D(ENTRADA[1]), .Q(SAIDA[1]));  // open: Qn, preset, en, reset
  D_Flip_Flop d_ff_8 (.clk(Clock), .D(ENTRADA[0]), .Q(SAIDA[0]));  // open: Qn, preset, en, reset
endmodule

module Banco_de_Registrador (
  input  [7:0] Rx,
  input  [3:0] Rx_select,
  input  [7:0] Data_IN,
  input  [7:0] Ry,
  input  [3:0] Ry_select,
  input  Write,
  input  [3:0] Write_select
);

  wire demultiplexer_1_out0, demultiplexer_1_out1, demultiplexer_1_out2, demultiplexer_1_out3,
       demultiplexer_1_out4, demultiplexer_1_out5, demultiplexer_1_out6, demultiplexer_1_out7,
       demultiplexer_1_out8, demultiplexer_1_out9, demultiplexer_1_out11, demultiplexer_1_out12,
       demultiplexer_1_out13, demultiplexer_1_out14, demultiplexer_1_out15;
  wire [3:0] undriven, undriven_2;
  wire [7:0] multiplexer_1_out, multiplexer_2_out, register_1_q, register_2_q, register_3_q, register_4_q,
       register_5_q, register_6_q, register_7_q, register_8_q, register_9_q, register_10_q, register_11_q,
       register_12_q, register_13_q, register_14_q, register_15_q, register_16_q;

  Demultiplexer #(.select(4)) demultiplexer_1 (
    .out0(demultiplexer_1_out0), .out1(demultiplexer_1_out1), .out2(demultiplexer_1_out2),
    .out3(demultiplexer_1_out3), .out4(demultiplexer_1_out4), .out5(demultiplexer_1_out5),
    .out6(demultiplexer_1_out6), .out7(demultiplexer_1_out7), .out8(demultiplexer_1_out8),
    .out9(demultiplexer_1_out9), .out10(demultiplexer_1_out9), .out11(demultiplexer_1_out11),
    .out12(demultiplexer_1_out12), .out13(demultiplexer_1_out13), .out14(demultiplexer_1_out14),
    .out15(demultiplexer_1_out15), .in(Write), .sel(Write_select));  // open: en
  Register register_1 (.D(Data_IN), .en(demultiplexer_1_out0), .Q(register_1_q));  // open: clk, clr
  Register register_2 (.D(Data_IN), .en(demultiplexer_1_out1), .Q(register_2_q));  // open: clk, clr
  Register register_3 (.D(Data_IN), .en(demultiplexer_1_out2), .Q(register_3_q));  // open: clk, clr
  Register register_4 (.D(Data_IN), .en(demultiplexer_1_out3), .Q(register_4_q));  // open: clk, clr
  Register register_5 (.D(Data_IN), .en(demultiplexer_1_out4), .Q(register_5_q));  // open: clk, clr
  Register register_6 (.D(Data_IN), .en(demultiplexer_1_out5), .Q(register_6_q));  // open: clk, clr
  Register register_7 (.D(Data_IN), .en(demultiplexer_1_out6), .Q(register_7_q));  // open: clk, clr
  Register register_8 (.D(Data_IN), .en(demultiplexer_1_out7), .Q(register_8_q));  // open: clk, clr
  Register register_9 (.D(Data_IN), .en(demultiplexer_1_out8), .Q(register_9_q));  // open: clk, clr
  Register register_10 (.D(Data_IN), .en(demultiplexer_1_out9), .Q(register_10_q));  // open: clk, clr
  Register register_11 (.D(Data_IN), .en(demultiplexer_1_out9), .Q(register_11_q));  // open: clk, clr
  Register register_12 (.D(Data_IN), .en(demultiplexer_1_out11), .Q(register_12_q));  // open: clk, clr
  Register register_13 (.D(Data_IN), .en(demultiplexer_1_out12), .Q(register_13_q));  // open: clk, clr
  Register register_14 (.D(Data_IN), .en(demultiplexer_1_out13), .Q(register_14_q));  // open: clk, clr
  Register register_15 (.D(Data_IN), .en(demultiplexer_1_out14), .Q(register_15_q));  // open: clk, clr
  Register register_16 (.D(Data_IN), .en(demultiplexer_1_out15), .Q(register_16_q));  // open: clk, clr
  Multiplexer #(.select(4), .width(8)) multiplexer_1 (
    .in0(register_1_q), .in1(register_2_q), .in2(register_3_q), .in3(register_4_q), .in4(register_5_q),
    .in5(register_6_q), .in6(register_7_q), .in7(register_8_q), .in8(register_9_q), .in9(register_10_q),
    .in10(register_11_q), .in11(register_12_q), .in12(register_13_q), .in13(register_14_q),
    .in14(register_15_q), .in15(register_16_q), .out(multiplexer_1_out), .sel(undriven));  // open: en
  Multiplexer #(.select(4), .width(8)) multiplexer_2 (
    .in0(register_1_q), .in1(register_2_q), .in2(register_3_q), .in3(register_4_q), .in4(register_5_q),
    .in5(register_6_q), .in6(register_7_q), .in7(register_8_q), .in8(register_9_q), .in9(register_10_q),
    .in10(register_11_q), .in11(register_12_q), .in12(register_13_q), .in13(register_14_q),
    .in14(register_15_q), .in15(register_16_q), .out(multiplexer_2_out), .sel(undriven_2));  // open: en
endmodule

module Somador_8_bits (
  input  inteiro,
  input  in_2,
  input  in_3,
  input  in_4,
  input  in_5,
  input  in_6,
  input  in_7,
  input  in_8,
  input  in_9,
  input  in_10,
  input  in_11,
  input  in_12,
  input  in_13,
  input  in_14,
  input  in_15,
  input  in_16,
  input  in_17,
  input  overflow,
  input  in_19,
  input  in_20,
  input  in_21,
  input  in_22,
  input  in_23,
  input  in_24,
  input  in_25,
  input  in_26
);

  wire adder_2_cout, adder_3_cout, adder_4_cout, adder_5_cout, adder_6_cout, adder_7_cout, adder_8_cout;

  Adder #(.width(1)) adder_1 (.a(in_10), .b(in_2), .out(in_19), .cin(adder_2_cout), .cout(overflow));
  Adder #(.width(1)) adder_2 (.a(in_11), .b(in_3), .out(in_20), .cin(adder_3_cout), .cout(adder_2_cout));
  Adder #(.width(1)) adder_3 (.a(in_12), .b(in_4), .out(in_21), .cin(adder_4_cout), .cout(adder_3_cout));
  Adder #(.width(1)) adder_4 (.a(in_13), .b(in_5), .out(in_22), .cin(adder_5_cout), .cout(adder_4_cout));
  Adder #(.width(1)) adder_5 (.a(in_14), .b(in_6), .out(in_23), .cin(adder_6_cout), .cout(adder_5_cout));
  Adder #(.width(1)) adder_6 (.a(in_15), .b(in_7), .out(in_24), .cin(adder_7_cout), .cout(adder_6_cout));
  Adder #(.width(1)) adder_7 (.a(in_16), .b(in_8), .out(in_25), .cin(adder_8_cout), .cout(adder_7_cout));
  Adder #(.width(1)) adder_8 (.a(in_17), .b(in_9), .out(in_26), .cin(inteiro), .cout(adder_8_cout));
endmodule

module ULA (
  input  [7:0] Reg_a0,
  input  [7:0] Reg_a1,
  input  OE,
  output [7:0] Dout,
  output [7:0] ULA_resultado,
  output CarryOut
);

  Adder adder_1 (.a(Reg_a0), .b(Reg_a1), .out(ULA_resultado), .cout(CarryOut));  // open: cin
  Subtractor subtractor_1 ();  // open: a, b, out, bin, bout
  assign Dout = OE ? ULA_resultado : 8'bz;  // Controlled_Buffer controlled_buffer_1
endmodule
